// Logisim project single_cycle_cpu.circ as structural Verilog: 22 circuits, main circuit Cpu
module Cpu (
  output [1:0] out_1,
  output [31:0] out_2,
  output [31:0] out_3,
  output [31:0] out_4
);

  wire and_1_out, branchlogic_1_branch, clk, clr, controlunit_1_alusrc, controlunit_1_branch,
       controlunit_1_jump, controlunit_1_memreadwrite, controlunit_1_regwrite, logic_unit_1_zero, or_1_out;
  wire [0:0] instrdecoder_1_funct3;
  wire [1:0] instrdecoder_1_funct3_2;
  wire [3:0] alucontrol_1_alucontrol, multiplexer_3_out_2, multiplexer_3_out_3, multiplexer_3_out_4,
       multiplexer_3_out_5, registers_1_rs1_out, registers_1_rs1_out_2, registers_1_rs1_out_3,
       registers_1_rs1_out_4, registers_1_rs1_out_5, registers_1_rs1_out_6, registers_1_rs1_out_7,
       registers_1_rs1_out_8, registers_1_rs2_out_2, registers_1_rs2_out_3, registers_1_rs2_out_4,
       registers_1_rs2_out_5;
  wire [4:0] instrdecoder_1_rd, instrdecoder_1_rs1, instrdecoder_1_rs2;
  wire [6:0] instrdecoder_1_funct7;
  wire [15:0] multiplexer_3_out, registers_1_rs2_out;
  wire [31:0] immgen_1_immediate, logic_unit_1_d_out, multiplexer_2_out, shifter_1_out, z28x4mem_1_read_data,
       z32b_adder_1_sum, z32b_adder_2_sum;

  Clock clock_1 (.out(clk));
  Button button_1 (.out(clr));
  PC pc_1 (.d_out(out_3), .clr(clr), .clk(clk), .d_in(out_2));
  Multiplexer #(.width(32), .enable("false")) multiplexer_1 (
    .in0(z32b_adder_1_sum), .in1(z32b_adder_2_sum), .out(out_2), .sel(or_1_out));
  or or_1 (or_1_out, and_1_out, controlunit_1_jump);
  and and_1 (and_1_out, controlunit_1_branch, branchlogic_1_branch);
  z32B_Adder z32b_adder_1 (.a(out_3), .sum(z32b_adder_1_sum), .b(32'h4));  // open: c_out, c_in
  InstrMem instrmem_1 (.instruction(out_4), .readAddr(out_3));
  Hex_Digit_Display hex_digit_display_1 (.value(multiplexer_3_out_5));  // open: dp
  ControlUnit controlunit_1 (
    .ALUSrc(controlunit_1_alusrc), .instruction(out_4), .Jump(controlunit_1_jump),
    .RegWrite(controlunit_1_regwrite), .MemReadWrite(controlunit_1_memreadwrite),
    .Branch(controlunit_1_branch), .MemDest(out_1));  // open: out_2
  InstrDecoder instrdecoder_1 (
    .rs2(instrdecoder_1_rs2), .rs1(instrdecoder_1_rs1),
    .funct3({instrdecoder_1_funct3_2, instrdecoder_1_funct3[0]}), .rd(instrdecoder_1_rd),
    .instruction(out_4), .funct7(instrdecoder_1_funct7));  // open: opcode
  Hex_Digit_Display hex_digit_display_2 (.value(multiplexer_3_out_3));  // open: dp
  Hex_Digit_Display hex_digit_display_3 (.value(multiplexer_3_out_4));  // open: dp
  Shifter #(.width(32)) shifter_1 (.in(immgen_1_immediate), .\dist (5'b00001), .out(shifter_1_out));
  ImmGen immgen_1 (.immediate(immgen_1_immediate), .instruction(out_4));
  Hex_Digit_Display hex_digit_display_4 (.value(multiplexer_3_out[15:12]));  // open: dp
  Hex_Digit_Display hex_digit_display_5 (.value(multiplexer_3_out_2));  // open: dp
  z32B_Adder z32b_adder_2 (.a(z32b_adder_1_sum), .sum(z32b_adder_2_sum), .b(shifter_1_out));  // open: c_out, c_in
  Hex_Digit_Display hex_digit_display_6 (.value(multiplexer_3_out[11:8]));  // open: dp
  Hex_Digit_Display hex_digit_display_7 (.value(multiplexer_3_out[7:4]));  // open: dp
  Hex_Digit_Display hex_digit_display_8 (.value(multiplexer_3_out[3:0]));  // open: dp
  Registers registers_1 (
    .read_address(instrdecoder_1_rd),
    .rs2_out({registers_1_rs2_out_5, registers_1_rs2_out_4, registers_1_rs2_out_3, registers_1_rs2_out_2, registers_1_rs2_out}),
    .rs2_address(instrdecoder_1_rs2),
    .rs1_out({registers_1_rs1_out_4, registers_1_rs1_out_3, registers_1_rs1_out_2, registers_1_rs1_out, registers_1_rs1_out_5, registers_1_rs1_out_6, registers_1_rs1_out_7, registers_1_rs1_out_8}),
    .write_enable(controlunit_1_regwrite),
    .data_in({multiplexer_3_out_5, multiplexer_3_out_4, multiplexer_3_out_3, multiplexer_3_out_2, multiplexer_3_out}),
    .rs1_address(instrdecoder_1_rs1), .clk(clk), .clr(clr));
  ALUControl alucontrol_1 (
    .ALUControl(alucontrol_1_alucontrol), .instruction(out_4), .funct7(instrdecoder_1_funct7),
    .funct3({instrdecoder_1_funct3_2, instrdecoder_1_funct3[0]}));
  Multiplexer #(.width(32), .enable("false")) multiplexer_2 (
    .in0({registers_1_rs2_out_5, registers_1_rs2_out_4, registers_1_rs2_out_3, registers_1_rs2_out_2, registers_1_rs2_out}),
    .in1(immgen_1_immediate), .out(multiplexer_2_out), .sel(controlunit_1_alusrc));
  Hex_Digit_Display hex_digit_display_9 (.value(registers_1_rs1_out_4));  // open: dp
  Hex_Digit_Display hex_digit_display_10 (.value(registers_1_rs1_out_3));  // open: dp
  Logic_Unit logic_unit_1 (
    .d_out(logic_unit_1_d_out), .d_in_b(multiplexer_2_out), .ALU_selection(alucontrol_1_alucontrol),
    .zero(logic_unit_1_zero),
    .d_in_a({registers_1_rs1_out_4, registers_1_rs1_out_3, registers_1_rs1_out_2, registers_1_rs1_out, registers_1_rs1_out_5, registers_1_rs1_out_6, registers_1_rs1_out_7, registers_1_rs1_out_8}));  // open: overflow
  Hex_Digit_Display hex_digit_display_11 (.value(registers_1_rs1_out_2));  // open: dp
  Hex_Digit_Display hex_digit_display_12 (.value(registers_1_rs1_out));  // open: dp
  Hex_Digit_Display hex_digit_display_13 (.value(registers_1_rs1_out_5));  // open: dp
  Hex_Digit_Display hex_digit_display_14 (.value(registers_1_rs1_out_6));  // open: dp
  BranchLogic branchlogic_1 (
    .branch(branchlogic_1_branch), .data(logic_unit_1_d_out),
    .funct3({instrdecoder_1_funct3_2, instrdecoder_1_funct3[0]}), .comp(logic_unit_1_zero));
  Hex_Digit_Display hex_digit_display_15 (.value(logic_unit_1_d_out[31:28]));  // open: dp
  Hex_Digit_Display hex_digit_display_16 (.value(registers_1_rs1_out_7));  // open: dp
  Hex_Digit_Display hex_digit_display_17 (.value(registers_1_rs1_out_8));  // open: dp
  Hex_Digit_Display hex_digit_display_18 (.value(logic_unit_1_d_out[27:24]));  // open: dp
  Hex_Digit_Display hex_digit_display_19 (.value(logic_unit_1_d_out[23:20]));  // open: dp
  Hex_Digit_Display hex_digit_display_20 (.value(registers_1_rs2_out_5));  // open: dp
  Hex_Digit_Display hex_digit_display_21 (.value(registers_1_rs2_out_4));  // open: dp
  z28x4Mem z28x4mem_1 (
    .addr(logic_unit_1_d_out), .write_enable(controlunit_1_memreadwrite),
    .write_data({registers_1_rs2_out_5, registers_1_rs2_out_4, registers_1_rs2_out_3, registers_1_rs2_out_2, registers_1_rs2_out}),
    .access_size(instrdecoder_1_funct3_2), .clk(clk), .read_data(z28x4mem_1_read_data));
  Hex_Digit_Display hex_digit_display_22 (.value(logic_unit_1_d_out[19:16]));  // open: dp
  Hex_Digit_Display hex_digit_display_23 (.value(logic_unit_1_d_out[15:12]));  // open: dp
  Hex_Digit_Display hex_digit_display_24 (.value(registers_1_rs2_out_3));  // open: dp
  Hex_Digit_Display hex_digit_display_25 (.value(registers_1_rs2_out_2));  // open: dp
  Multiplexer #(.select(2), .width(32), .enable("false")) multiplexer_3 (
    .in0(logic_unit_1_d_out), .in1(z28x4mem_1_read_data), .in2(z32b_adder_1_sum), .in3(z32b_adder_1_sum),
    .out({multiplexer_3_out_5, multiplexer_3_out_4, multiplexer_3_out_3, multiplexer_3_out_2, multiplexer_3_out}),
    .sel(out_1));
  Hex_Digit_Display hex_digit_display_26 (.value(logic_unit_1_d_out[11:8]));  // open: dp
  Hex_Digit_Display hex_digit_display_27 (.value(logic_unit_1_d_out[7:4]));  // open: dp
  Hex_Digit_Display hex_digit_display_28 (.value(registers_1_rs2_out[11:8]));  // open: dp
  Hex_Digit_Display hex_digit_display_29 (.value(registers_1_rs2_out[15:12]));  // open: dp
  Hex_Digit_Display hex_digit_display_30 (.value(logic_unit_1_d_out[3:0]));  // open: dp
  Hex_Digit_Display hex_digit_display_31 (.value(registers_1_rs2_out[7:4]));  // open: dp
  Hex_Digit_Display hex_digit_display_32 (.value(registers_1_rs2_out[3:0]));  // open: dp

  // Notes on the sheet:
  //   ALU Out
endmodule

module Registers (
  input  [31:0] data_in,
  input  [4:0] rs1_address,
  input  [4:0] rs2_address,
  input  [4:0] read_address,
  input  write_enable,
  input  clk,
  input  clr,
  output [31:0] rs1_out,
  output [31:0] rs2_out
);

  wire decoder_1_out0, decoder_1_out1, decoder_1_out2, decoder_1_out3, decoder_1_out4, decoder_1_out5,
       decoder_1_out6, decoder_1_out7, decoder_1_out8, decoder_1_out9, decoder_1_out10, decoder_1_out11,
       decoder_1_out12, decoder_1_out13, decoder_1_out14, decoder_1_out15, decoder_1_out16, decoder_1_out17,
       decoder_1_out18, decoder_1_out19, decoder_1_out20, decoder_1_out21, decoder_1_out22, decoder_1_out23,
       decoder_1_out24, decoder_1_out25, decoder_1_out26, decoder_1_out27, decoder_1_out28, decoder_1_out29,
       decoder_1_out30, decoder_1_out31;
  wire [31:0] x0_q, x1_q, x2_q, x3_q, x4_q, x5_q, x6_q, x7_q, x8_q, x9_q, x10_q, x11_q, x12_q, x13_q, x14_q,
       x15_q, x16_q, x17_q, x18_q, x19_q, x20_q, x21_q, x22_q, x23_q, x24_q, x25_q, x26_q, x27_q, x28_q,
       x29_q, x30_q, x31_q;

  Decoder #(.select(5)) decoder_1 (
    .out0(decoder_1_out0), .out1(decoder_1_out1), .out2(decoder_1_out2), .out3(decoder_1_out3),
    .out4(decoder_1_out4), .out5(decoder_1_out5), .out6(decoder_1_out6), .out7(decoder_1_out7),
    .out8(decoder_1_out8), .out9(decoder_1_out9), .out10(decoder_1_out10), .out11(decoder_1_out11),
    .out12(decoder_1_out12), .out13(decoder_1_out13), .out14(decoder_1_out14), .out15(decoder_1_out15),
    .out16(decoder_1_out16), .out17(decoder_1_out17), .out18(decoder_1_out18), .out19(decoder_1_out19),
    .out20(decoder_1_out20), .out21(decoder_1_out21), .out22(decoder_1_out22), .out23(decoder_1_out23),
    .out24(decoder_1_out24), .out25(decoder_1_out25), .out26(decoder_1_out26), .out27(decoder_1_out27),
    .out28(decoder_1_out28), .out29(decoder_1_out29), .out30(decoder_1_out30), .out31(decoder_1_out31),
    .sel(read_address), .en(write_enable));
  Register #(.width(32)) x0 (.D({32{1'b0}}), .en(decoder_1_out0), .clk(clk), .Q(x0_q), .clr(clr));
  Register #(.width(32)) x1 (.D(data_in), .en(decoder_1_out1), .clk(clk), .Q(x1_q), .clr(clr));
  Register #(.width(32)) x2 (.D(data_in), .en(decoder_1_out2), .clk(clk), .Q(x2_q), .clr(clr));
  Register #(.width(32)) x3 (.D(data_in), .en(decoder_1_out3), .clk(clk), .Q(x3_q), .clr(clr));
  Register #(.width(32)) x4 (.D(data_in), .en(decoder_1_out4), .clk(clk), .Q(x4_q), .clr(clr));
  Register #(.width(32)) x5 (.D(data_in), .en(decoder_1_out5), .clk(clk), .Q(x5_q), .clr(clr));
  Register #(.width(32)) x6 (.D(data_in), .en(decoder_1_out6), .clk(clk), .Q(x6_q), .clr(clr));
  Register #(.width(32)) x7 (.D(data_in), .en(decoder_1_out7), .clk(clk), .Q(x7_q), .clr(clr));
  Register #(.width(32)) x8 (.D(data_in), .en(decoder_1_out8), .clk(clk), .Q(x8_q), .clr(clr));
  Register #(.width(32)) x9 (.D(data_in), .en(decoder_1_out9), .clk(clk), .Q(x9_q), .clr(clr));
  Register #(.width(32)) x10 (.D(data_in), .en(decoder_1_out10), .clk(clk), .Q(x10_q), .clr(clr));
  Register #(.width(32)) x11 (.D(data_in), .en(decoder_1_out11), .clk(clk), .Q(x11_q), .clr(clr));
  Register #(.width(32)) x12 (.D(data_in), .en(decoder_1_out12), .clk(clk), .Q(x12_q), .clr(clr));
  Register #(.width(32)) x13 (.D(data_in), .en(decoder_1_out13), .clk(clk), .Q(x13_q), .clr(clr));
  Register #(.width(32)) x14 (.D(data_in), .en(decoder_1_out14), .clk(clk), .Q(x14_q), .clr(clr));
  Register #(.width(32)) x15 (.D(data_in), .en(decoder_1_out15), .clk(clk), .Q(x15_q), .clr(clr));
  Register #(.width(32)) x16 (.D(data_in), .en(decoder_1_out16), .clk(clk), .Q(x16_q), .clr(clr));
  Register #(.width(32)) x17 (.D(data_in), .en(decoder_1_out17), .clk(clk), .Q(x17_q), .clr(clr));
  Register #(.width(32)) x18 (.D(data_in), .en(decoder_1_out18), .clk(clk), .Q(x18_q), .clr(clr));
  Register #(.width(32)) x19 (.D(data_in), .en(decoder_1_out19), .clk(clk), .Q(x19_q), .clr(clr));
  Register #(.width(32)) x20 (.D(data_in), .en(decoder_1_out20), .clk(clk), .Q(x20_q), .clr(clr));
  Register #(.width(32)) x21 (.D(data_in), .en(decoder_1_out21), .clk(clk), .Q(x21_q), .clr(clr));
  Register #(.width(32)) x22 (.D(data_in), .en(decoder_1_out22), .clk(clk), .Q(x22_q), .clr(clr));
  Register #(.width(32)) x23 (.D(data_in), .en(decoder_1_out23), .clk(clk), .Q(x23_q), .clr(clr));
  Register #(.width(32)) x24 (.D(data_in), .en(decoder_1_out24), .clk(clk), .Q(x24_q), .clr(clr));
  Register #(.width(32)) x25 (.D(data_in), .en(decoder_1_out25), .clk(clk), .Q(x25_q), .clr(clr));
  Register #(.width(32)) x26 (.D(data_in), .en(decoder_1_out26), .clk(clk), .Q(x26_q), .clr(clr));
  Register #(.width(32)) x27 (.D(data_in), .en(decoder_1_out27), .clk(clk), .Q(x27_q), .clr(clr));
  Register #(.width(32)) x28 (.D(data_in), .en(decoder_1_out28), .clk(clk), .Q(x28_q), .clr(clr));
  Register #(.width(32)) x29 (.D(data_in), .en(decoder_1_out29), .clk(clk), .Q(x29_q), .clr(clr));
  Register #(.width(32)) x30 (.D(data_in), .en(decoder_1_out30), .clk(clk), .Q(x30_q), .clr(clr));
  Register #(.width(32)) x31 (.D(data_in), .en(decoder_1_out31), .clk(clk), .Q(x31_q), .clr(clr));
  Multiplexer #(.select(5), .width(32), .enable("false")) multiplexer_1 (
    .in0(x0_q), .in1(x1_q), .in2(x2_q), .in3(x3_q), .in4(x4_q), .in5(x5_q), .in6(x6_q), .in7(x7_q),
    .in8(x8_q), .in9(x9_q), .in10(x10_q), .in11(x11_q), .in12(x12_q), .in13(x13_q), .in14(x14_q),
    .in15(x15_q), .in16(x16_q), .in17(x17_q), .in18(x18_q), .in19(x19_q), .in20(x20_q), .in21(x21_q),
    .in22(x22_q), .in23(x23_q), .in24(x24_q), .in25(x25_q), .in26(x26_q), .in27(x27_q), .in28(x28_q),
    .in29(x29_q), .in30(x30_q), .in31(x31_q), .out(rs1_out), .sel(rs1_address));
  Multiplexer #(.select(5), .width(32), .enable("false")) multiplexer_2 (
    .in0(x0_q), .in1(x1_q), .in2(x2_q), .in3(x3_q), .in4(x4_q), .in5(x5_q), .in6(x6_q), .in7(x7_q),
    .in8(x8_q), .in9(x9_q), .in10(x10_q), .in11(x11_q), .in12(x12_q), .in13(x13_q), .in14(x14_q),
    .in15(x15_q), .in16(x16_q), .in17(x17_q), .in18(x18_q), .in19(x19_q), .in20(x20_q), .in21(x21_q),
    .in22(x22_q), .in23(x23_q), .in24(x24_q), .in25(x25_q), .in26(x26_q), .in27(x27_q), .in28(x28_q),
    .in29(x29_q), .in30(x30_q), .in31(x31_q), .out(rs2_out), .sel(rs2_address));

  // Other names for the same wires on the sheet: d_in[31:0] = data_in
endmodule

module Logic_Unit (
  input  [31:0] d_in_a,
  input  [31:0] d_in_b,
  input  [3:0] ALU_selection,
  output overflow,
  output [31:0] d_out,
  output zero
);

  wire comparatorunit_1_comp;
  wire [31:0] bit_extender_1_out, comparatorunit_1_sum, logic_1_d_out, shifterunit_1_d_out;

  ShifterUnit shifterunit_1 (.a(d_in_a), .op(ALU_selection[1:0]), .amt(d_in_b), .d_out(shifterunit_1_d_out));
  Logic logic_1 (.a(d_in_a), .b(d_in_b), .sel(ALU_selection[1:0]), .d_out(logic_1_d_out));
  ComparatorUnit comparatorunit_1 (
    .a(d_in_a), .b(d_in_b), .sub_control(ALU_selection[0]), .sum(comparatorunit_1_sum), .overflow(overflow),
    .comp(comparatorunit_1_comp));
  assign bit_extender_1_out = {{31{comparatorunit_1_comp}}, comparatorunit_1_comp};  // Bit_Extender bit_extender_1
  Multiplexer #(.select(2), .width(32), .enable("false")) multiplexer_1 (
    .in0(shifterunit_1_d_out), .in1(bit_extender_1_out), .in2(comparatorunit_1_sum), .in3(logic_1_d_out),
    .out(d_out), .sel(ALU_selection[3:2]));
  Comparator #(.width(32)) comparator_1 (.a(d_out), .b({32{1'b0}}), .eq(zero));  // open: gt, lt

  // Other names for the same wires on the sheet: alu_out[31:0] = d_out
endmodule

module z1B_Adder (
  input  a,
  input  b,
  input  c_in,
  output sum,
  output c_out
);

  wire and_1_out, and_2_out, xor_1_out;

  xor xor_1 (xor_1_out, a, b);
  xor xor_2 (sum, xor_1_out, c_in);
  and and_1 (and_1_out, a, b);
  and and_2 (and_2_out, xor_1_out, c_in);
  or or_1 (c_out, and_1_out, and_2_out);
endmodule

module z2B_Adder (
  input  [1:0] a,
  input  [1:0] b,
  input  c_in,
  output [1:0] sum,
  output c_out
);

  wire z1b_adder_1_c_out;

  z1B_Adder z1b_adder_1 (.a(a[0]), .b(b[0]), .c_in(c_in), .sum(sum[0]), .c_out(z1b_adder_1_c_out));
  z1B_Adder z1b_adder_2 (.a(a[1]), .b(b[1]), .c_in(z1b_adder_1_c_out), .sum(sum[1]), .c_out(c_out));
endmodule

module z4B_Adder (
  input  [3:0] a,
  input  [3:0] b,
  input  c_in,
  output [3:0] sum,
  output c_out
);

  wire z2b_adder_1_c_out;

  z2B_Adder z2b_adder_1 (.a(a[1:0]), .b(b[1:0]), .c_in(c_in), .sum(sum[1:0]), .c_out(z2b_adder_1_c_out));
  z2B_Adder z2b_adder_2 (.a(a[3:2]), .b(b[3:2]), .c_in(z2b_adder_1_c_out), .sum(sum[3:2]), .c_out(c_out));
endmodule

module z8B_Adder (
  input  [7:0] a,
  input  [7:0] b,
  input  c_in,
  output [7:0] sum,
  output c_out
);

  wire z4b_adder_1_c_out;

  z4B_Adder z4b_adder_1 (.a(a[3:0]), .b(b[3:0]), .c_in(c_in), .sum(sum[3:0]), .c_out(z4b_adder_1_c_out));
  z4B_Adder z4b_adder_2 (.a(a[7:4]), .b(b[7:4]), .c_in(z4b_adder_1_c_out), .sum(sum[7:4]), .c_out(c_out));
endmodule

module z16B_Adder (
  input  [15:0] a,
  input  [15:0] b,
  input  c_in,
  output [15:0] sum,
  output c_out
);

  wire z8b_adder_1_c_out;

  z8B_Adder z8b_adder_1 (.a(a[7:0]), .b(b[7:0]), .c_in(c_in), .sum(sum[7:0]), .c_out(z8b_adder_1_c_out));
  z8B_Adder z8b_adder_2 (.a(a[15:8]), .b(b[15:8]), .c_in(z8b_adder_1_c_out), .sum(sum[15:8]), .c_out(c_out));
endmodule

module z32B_Adder (
  input  [31:0] a,
  input  [31:0] b,
  input  c_in,
  output [31:0] sum,
  output c_out
);

  wire z16b_adder_1_c_out;

  z16B_Adder z16b_adder_1 (.a(a[15:0]), .b(b[15:0]), .c_in(c_in), .sum(sum[15:0]), .c_out(z16b_adder_1_c_out));
  z16B_Adder z16b_adder_2 (.a(a[31:16]), .b(b[31:16]), .c_in(z16b_adder_1_c_out), .sum(sum[31:16]), .c_out(c_out));
endmodule

module ImmGen (
  input  [31:0] instruction,
  output [31:0] immediate
);

  wire and_1_out, and_2_out, and_3_out, and_4_out, and_5_out, and_6_out;
  wire [31:0] and_7_out, and_8_out, and_9_out, and_10_out, and_11_out, and_12_out, bit_extender_1_out,
       bit_extender_2_out, bit_extender_3_out, bit_extender_4_out, bit_extender_5_out, bit_extender_6_out,
       bit_extender_7_out, bit_extender_8_out, bit_extender_9_out, bit_extender_10_out, bit_extender_11_out;

  and and_1 (and_1_out, instruction[0], instruction[1], ~instruction[2], ~instruction[3], instruction[4], instruction[5], ~instruction[6]);  // AND_Gate
  and and_2 (and_2_out, instruction[0], instruction[1], ~instruction[2], ~instruction[3], 1'b1, ~instruction[5], ~instruction[6]);  // AND_Gate
  and and_3 (and_3_out, instruction[0], instruction[1], ~instruction[2], ~instruction[3], ~instruction[4], instruction[5], ~instruction[6]);  // AND_Gate
  and and_4 (and_4_out, instruction[0], instruction[1], ~instruction[2], ~instruction[3], ~instruction[4], instruction[5], instruction[6]);  // AND_Gate
  and and_5 (and_5_out, instruction[0], instruction[1], instruction[2], ~instruction[3], instruction[4], 1'b1, ~instruction[6]);  // AND_Gate
  and and_6 (and_6_out, instruction[0], instruction[1], instruction[2], instruction[3], ~instruction[4], instruction[5], instruction[6]);  // AND_Gate
  assign bit_extender_1_out = {{31{and_1_out}}, and_1_out};  // Bit_Extender bit_extender_1
  assign bit_extender_2_out = {{20{instruction[31]}}, instruction[31:20]};  // Bit_Extender bit_extender_2
  assign bit_extender_3_out = {{31{and_2_out}}, and_2_out};  // Bit_Extender bit_extender_3
  assign bit_extender_4_out = {{20{instruction[31]}}, {instruction[31:25], instruction[11:7]}};  // Bit_Extender bit_extender_4
  assign bit_extender_5_out = {{31{and_3_out}}, and_3_out};  // Bit_Extender bit_extender_5
  assign bit_extender_6_out = {{20{instruction[31]}}, {instruction[31], instruction[7], instruction[30:25], instruction[11:8]}};  // Bit_Extender bit_extender_6
  assign bit_extender_7_out = {{31{and_4_out}}, and_4_out};  // Bit_Extender bit_extender_7
  assign bit_extender_8_out = {{12{instruction[31]}}, instruction[31:12]};  // Bit_Extender bit_extender_8
  assign bit_extender_9_out = {{31{and_5_out}}, and_5_out};  // Bit_Extender bit_extender_9
  assign and_7_out = bit_extender_1_out & {32{1'b0}};  // AND_Gate and_7, 32 bits wide
  assign and_8_out = bit_extender_2_out & bit_extender_3_out;  // AND_Gate and_8, 32 bits wide
  assign and_9_out = bit_extender_4_out & bit_extender_5_out;  // AND_Gate and_9, 32 bits wide
  assign and_10_out = bit_extender_6_out & bit_extender_7_out;  // AND_Gate and_10, 32 bits wide
  assign and_11_out = bit_extender_8_out & bit_extender_9_out;  // AND_Gate and_11, 32 bits wide
  assign bit_extender_10_out = {{12{instruction[31]}}, {instruction[31], instruction[19:12], instruction[20], instruction[30:21]}};  // Bit_Extender bit_extender_10
  assign bit_extender_11_out = {{31{and_6_out}}, and_6_out};  // Bit_Extender bit_extender_11
  assign and_12_out = bit_extender_10_out & bit_extender_11_out;  // AND_Gate and_12, 32 bits wide
  assign immediate = and_7_out | and_8_out | and_9_out | and_10_out | and_11_out | and_12_out;  // OR_Gate or_1, 32 bits wide

  // Notes on the sheet:
  //   R-Type
  //   I-Type
  //   S-Type
  //   B-Type
  //   U-Type
  //   J-Type
endmodule

module ControlUnit (
  input  [31:0] instruction,
  output [6:0] out_2,
  output RegWrite,
  output ALUSrc,
  output MemReadWrite,
  output Branch,
  output [1:0] MemDest,
  output Jump
);

  wire [6:0] and_1_out;

  and and_1 (and_1_out[0], instruction[0], instruction[1], ~instruction[2], ~instruction[3], instruction[4], instruction[5], ~instruction[6]);  // AND_Gate
  and and_2 (and_1_out[1], instruction[0], instruction[1], ~instruction[2], ~instruction[3], instruction[4], ~instruction[5], ~instruction[6]);  // AND_Gate
  and and_3 (and_1_out[2], instruction[0], instruction[1], ~instruction[2], ~instruction[3], ~instruction[4], ~instruction[5], ~instruction[6]);  // AND_Gate
  and and_4 (and_1_out[3], instruction[0], instruction[1], ~instruction[2], ~instruction[3], ~instruction[4], instruction[5], ~instruction[6]);  // AND_Gate
  and and_5 (and_1_out[4], instruction[0], instruction[1], ~instruction[2], ~instruction[3], ~instruction[4], instruction[5], instruction[6]);  // AND_Gate
  and and_6 (and_1_out[5], instruction[0], instruction[1], instruction[2], ~instruction[3], instruction[4], 1'b1, ~instruction[6]);  // AND_Gate
  and and_7 (and_1_out[6], instruction[0], instruction[1], instruction[2], instruction[3], ~instruction[4], instruction[5], instruction[6]);  // AND_Gate
  ROM #(.addrWidth(7), .dataWidth(7)) rom_1 (
    .addr(and_1_out), .data({Jump, MemDest, Branch, MemReadWrite, ALUSrc, RegWrite}));

  assign out_2 = instruction[6:0];

  // Other names for the same wires on the sheet: opcode[6:0] = instruction[6:0]

  // Notes on the sheet:
  //   R type
  //   I type
  //   I type (load)
  //   B Type
  //   J Type
  //   contents of rom_1 (hex, n*v repeats v):
  //   0 1 3 13 17 8 1 63 2 7*0 8 47*0 61
endmodule

module PC (
  input  [31:0] d_in,
  input  clk,
  input  clr,
  output [31:0] d_out
);

  Register #(.width(32)) register_1 (.D(d_in), .en(1'b1), .clk(clk), .Q(d_out), .clr(clr));
endmodule

module InstrMem (
  input  [31:0] readAddr,
  output [31:0] instruction
);

  ROM #(.addrWidth(24), .dataWidth(32)) rom_1 (.addr(readAddr[25:2]), .data(instruction));

  // Notes on the sheet:
  //   contents of rom_1 (hex, n*v repeats v):
  //   a00093 a00113 208463 6f00193 de00193 302023 2203 fe209ae3 8002ef 6300313 3700313 100393
endmodule

module ALUControl (
  input  [2:0] funct3,
  input  [6:0] funct7,
  input  [31:0] instruction,
  output [3:0] ALUControl
);

  wire and_1_out, and_2_out, and_3_out, and_4_out, and_6_out, and_7_out, and_8_out, nor_1_out, or_1_out;
  wire [1:0] or_2_out;
  wire [1:1] and_10_out;
  wire [3:0] multiplexer_1_out, multiplexer_2_out, multiplexer_3_out;
  wire [3:3] and_9_out;

  Multiplexer #(.select(3), .width(4), .enable("false")) multiplexer_1 (
    .in0(4'b1000), .in1(4'b0001), .in2(4'b0110), .in3(4'b0101), .in4(4'b1111), .in5(4'b0011), .in6(4'b1101),
    .in7(4'b1100), .out(multiplexer_1_out), .sel(funct3));
  or or_1 (or_1_out, funct7[0], funct7[1], funct7[2], funct7[3], funct7[4], funct7[5], funct7[6]);
  and and_1 (and_1_out, funct3[0], ~funct3[1], funct3[2]);  // AND_Gate
  and and_2 (and_2_out, instruction[0], instruction[1], ~instruction[2], ~instruction[3], instruction[4], ~instruction[5], ~instruction[6]);  // AND_Gate
  and and_3 (and_3_out, instruction[0], instruction[1], ~instruction[2], ~instruction[3], ~instruction[4], ~instruction[5], ~instruction[6]);  // AND_Gate
  and and_4 (and_4_out, instruction[0], instruction[1], ~instruction[2], ~instruction[3], ~instruction[4], instruction[5], ~instruction[6]);  // AND_Gate
  and and_5 (or_2_out[1], instruction[0], instruction[1], ~instruction[2], ~instruction[3], ~instruction[4], instruction[5], instruction[6]);  // AND_Gate
  and and_6 (and_6_out, instruction[0], instruction[1], instruction[2], instruction[3], ~instruction[4], instruction[5], instruction[6]);  // AND_Gate
  nor nor_1 (nor_1_out, funct3[0], funct3[1], funct3[2]);
  and and_7 (and_7_out, nor_1_out, or_1_out);
  and and_8 (and_8_out, and_1_out, or_1_out);
  and and_9 (and_9_out[3], and_7_out, ~and_2_out);  // AND_Gate
  and and_10 (and_10_out[1], and_8_out, ~and_2_out);  // AND_Gate
  or or_2 (or_2_out[0], and_3_out, and_4_out, and_6_out);
  Multiplexer #(.width(4), .enable("false")) multiplexer_2 (
    .in0(multiplexer_1_out), .in1({and_9_out[3], 1'b0, {2{and_9_out[3]}}}), .out(multiplexer_2_out),
    .sel(and_9_out[3]));
  Multiplexer #(.width(4), .enable("false")) multiplexer_3 (
    .in0(multiplexer_2_out), .in1({2'b00, {2{and_10_out[1]}}}), .out(multiplexer_3_out), .sel(and_10_out[1]));
  Multiplexer #(.select(2), .width(4), .enable("false")) multiplexer_4 (
    .in0(multiplexer_3_out), .in1(4'b1000), .in2(4'b0101), .in3(4'b0000), .out(ALUControl), .sel(or_2_out));
  Multiplexer #(.width(4), .enable("false")) multiplexer_5 ();  // open: in0, in1, out, sel
endmodule

module BranchLogic (
  input  comp,
  input  [2:0] funct3,
  input  [31:0] data,
  output branch
);

  ROM #(.addrWidth(5), .dataWidth(1)) rom_1 (.addr({data[0], funct3, comp}));  // open: data

  // Notes on the sheet:
  //   contents of rom_1 (hex, n*v repeats v):
  //   0 1 1 8*0 1 5*0 1 1
endmodule

module InstrDecoder (
  input  [31:0] instruction,
  output [6:0] opcode,
  output [4:0] rd,
  output [2:0] funct3,
  output [4:0] rs1,
  output [4:0] rs2,
  output [6:0] funct7
);


  assign funct3 = instruction[14:12];
  assign funct7 = instruction[31:25];
  assign opcode = instruction[6:0];
  assign rd = instruction[11:7];
  assign rs1 = instruction[19:15];
  assign rs2 = instruction[24:20];
endmodule

module z24x16Mem (
  input  wr_enable,
  input  [25:0] mem_sel,
  input  [3:0] sel,
  input  [31:0] write_data,
  input  clk,
  input  [1:0] access_size,
  output [31:0] read_data
);

  wire demultiplexer_1_out0, demultiplexer_1_out1, demultiplexer_1_out2, demultiplexer_1_out3,
       demultiplexer_1_out4, demultiplexer_1_out5, demultiplexer_1_out6, demultiplexer_1_out7,
       demultiplexer_1_out8, demultiplexer_1_out9, demultiplexer_1_out10, demultiplexer_1_out11,
       demultiplexer_1_out12, demultiplexer_1_out13, demultiplexer_1_out14, demultiplexer_1_out15, not_1_out,
       not_2_out, not_3_out, not_4_out, not_5_out, not_6_out, not_7_out, not_8_out, not_9_out, not_10_out,
       not_11_out, not_12_out, not_13_out, not_14_out, not_15_out, not_16_out;
  wire [3:0] multiplexer_1_out, multiplexer_2_out, multiplexer_3_out;
  wire [31:0] ram_1_dout, ram_2_dout, ram_3_dout, ram_4_dout, ram_5_dout, ram_6_dout, ram_7_dout, ram_8_dout,
       ram_9_dout, ram_10_dout, ram_11_dout, ram_12_dout, ram_13_dout, ram_14_dout, ram_15_dout, ram_16_dout;

  Multiplexer #(.select(2), .width(4), .enable("false")) multiplexer_1 (
    .in0(4'b1000), .in1(4'b0100), .in2(4'b0010), .in3(4'b0001), .out(multiplexer_1_out), .sel(mem_sel[1:0]));
  Multiplexer #(.width(4), .enable("false")) multiplexer_2 (
    .in0(4'b0011), .in1(4'b1100), .out(multiplexer_2_out), .sel(mem_sel[1]));
  Demultiplexer #(.select(4), .enable("false")) demultiplexer_1 (
    .out0(demultiplexer_1_out0), .out1(demultiplexer_1_out1), .out2(demultiplexer_1_out2),
    .out3(demultiplexer_1_out3), .out4(demultiplexer_1_out4), .out5(demultiplexer_1_out5),
    .out6(demultiplexer_1_out6), .out7(demultiplexer_1_out7), .out8(demultiplexer_1_out8),
    .out9(demultiplexer_1_out9), .out10(demultiplexer_1_out10), .out11(demultiplexer_1_out11),
    .out12(demultiplexer_1_out12), .out13(demultiplexer_1_out13), .out14(demultiplexer_1_out14),
    .out15(demultiplexer_1_out15), .in(wr_enable), .sel(sel));
  Multiplexer #(.select(2), .width(4), .enable("false")) multiplexer_3 (
    .in0(multiplexer_1_out), .in1(multiplexer_2_out), .in2(4'b1111), .in3(4'b1111), .out(multiplexer_3_out),
    .sel(access_size));
  RAM #(.addrWidth(24), .dataWidth(32), .databus("bibus"), .byteenables("byteEnables")) ram_1 (
    .addr(mem_sel[25:2]), .we(demultiplexer_1_out0), .oe(not_1_out), .clk(clk), .din(write_data),
    .dout(ram_1_dout), .be3(multiplexer_3_out[0]), .be2(multiplexer_3_out[1]), .be1(multiplexer_3_out[2]),
    .be0(multiplexer_3_out[3]));
  not not_1 (not_1_out, demultiplexer_1_out0);
  RAM #(.addrWidth(24), .dataWidth(32), .databus("bibus"), .byteenables("byteEnables")) ram_2 (
    .addr(mem_sel[25:2]), .we(demultiplexer_1_out1), .oe(not_2_out), .clk(clk), .din(write_data),
    .dout(ram_2_dout), .be3(multiplexer_3_out[0]), .be2(multiplexer_3_out[1]), .be1(multiplexer_3_out[2]),
    .be0(multiplexer_3_out[3]));
  not not_2 (not_2_out, demultiplexer_1_out1);
  RAM #(.addrWidth(24), .dataWidth(32), .databus("bibus"), .byteenables("byteEnables")) ram_3 (
    .addr(mem_sel[25:2]), .we(demultiplexer_1_out2), .oe(not_3_out), .clk(clk), .din(write_data),
    .dout(ram_3_dout), .be3(multiplexer_3_out[0]), .be2(multiplexer_3_out[1]), .be1(multiplexer_3_out[2]),
    .be0(multiplexer_3_out[3]));
  not not_3 (not_3_out, demultiplexer_1_out2);
  RAM #(.addrWidth(24), .dataWidth(32), .databus("bibus"), .byteenables("byteEnables")) ram_4 (
    .addr(mem_sel[25:2]), .we(demultiplexer_1_out3), .oe(not_4_out), .clk(clk), .din(write_data),
    .dout(ram_4_dout), .be3(multiplexer_3_out[0]), .be2(multiplexer_3_out[1]), .be1(multiplexer_3_out[2]),
    .be0(multiplexer_3_out[3]));
  not not_4 (not_4_out, demultiplexer_1_out3);
  RAM #(.addrWidth(24), .dataWidth(32), .databus("bibus"), .byteenables("byteEnables")) ram_5 (
    .addr(mem_sel[25:2]), .we(demultiplexer_1_out4), .oe(not_5_out), .clk(clk), .din(write_data),
    .dout(ram_5_dout), .be3(multiplexer_3_out[0]), .be2(multiplexer_3_out[1]), .be1(multiplexer_3_out[2]),
    .be0(multiplexer_3_out[3]));
  not not_5 (not_5_out, demultiplexer_1_out4);
  RAM #(.addrWidth(24), .dataWidth(32), .databus("bibus"), .byteenables("byteEnables")) ram_6 (
    .addr(mem_sel[25:2]), .we(demultiplexer_1_out5), .oe(not_6_out), .clk(clk), .din(write_data),
    .dout(ram_6_dout), .be3(multiplexer_3_out[0]), .be2(multiplexer_3_out[1]), .be1(multiplexer_3_out[2]),
    .be0(multiplexer_3_out[3]));
  not not_6 (not_6_out, demultiplexer_1_out5);
  RAM #(.addrWidth(24), .dataWidth(32), .databus("bibus"), .byteenables("byteEnables")) ram_7 (
    .addr(mem_sel[25:2]), .we(demultiplexer_1_out6), .oe(not_7_out), .clk(clk), .din(write_data),
    .dout(ram_7_dout), .be3(multiplexer_3_out[0]), .be2(multiplexer_3_out[1]), .be1(multiplexer_3_out[2]),
    .be0(multiplexer_3_out[3]));
  not not_7 (not_7_out, demultiplexer_1_out6);
  RAM #(.addrWidth(24), .dataWidth(32), .databus("bibus"), .byteenables("byteEnables")) ram_8 (
    .addr(mem_sel[25:2]), .we(demultiplexer_1_out7), .oe(not_8_out), .clk(clk), .din(write_data),
    .dout(ram_8_dout), .be3(multiplexer_3_out[0]), .be2(multiplexer_3_out[1]), .be1(multiplexer_3_out[2]),
    .be0(multiplexer_3_out[3]));
  not not_8 (not_8_out, demultiplexer_1_out7);
  RAM #(.addrWidth(24), .dataWidth(32), .databus("bibus"), .byteenables("byteEnables")) ram_9 (
    .addr(mem_sel[25:2]), .we(demultiplexer_1_out8), .oe(not_9_out), .clk(clk), .din(write_data),
    .dout(ram_9_dout), .be3(multiplexer_3_out[0]), .be2(multiplexer_3_out[1]), .be1(multiplexer_3_out[2]),
    .be0(multiplexer_3_out[3]));
  not not_9 (not_9_out, demultiplexer_1_out8);
  RAM #(.addrWidth(24), .dataWidth(32), .databus("bibus"), .byteenables("byteEnables")) ram_10 (
    .addr(mem_sel[25:2]), .we(demultiplexer_1_out9), .oe(not_10_out), .clk(clk), .din(write_data),
    .dout(ram_10_dout), .be3(multiplexer_3_out[0]), .be2(multiplexer_3_out[1]), .be1(multiplexer_3_out[2]),
    .be0(multiplexer_3_out[3]));
  not not_10 (not_10_out, demultiplexer_1_out9);
  RAM #(.addrWidth(24), .dataWidth(32), .databus("bibus"), .byteenables("byteEnables")) ram_11 (
    .addr(mem_sel[25:2]), .we(demultiplexer_1_out10), .oe(not_11_out), .clk(clk), .din(write_data),
    .dout(ram_11_dout), .be3(multiplexer_3_out[0]), .be2(multiplexer_3_out[1]), .be1(multiplexer_3_out[2]),
    .be0(multiplexer_3_out[3]));
  not not_11 (not_11_out, demultiplexer_1_out10);
  RAM #(.addrWidth(24), .dataWidth(32), .databus("bibus"), .byteenables("byteEnables")) ram_12 (
    .addr(mem_sel[25:2]), .we(demultiplexer_1_out11), .oe(not_12_out), .clk(clk), .din(write_data),
    .dout(ram_12_dout), .be3(multiplexer_3_out[0]), .be2(multiplexer_3_out[1]), .be1(multiplexer_3_out[2]),
    .be0(multiplexer_3_out[3]));
  not not_12 (not_12_out, demultiplexer_1_out11);
  RAM #(.addrWidth(24), .dataWidth(32), .databus("bibus"), .byteenables("byteEnables")) ram_13 (
    .addr(mem_sel[25:2]), .we(demultiplexer_1_out12), .oe(not_13_out), .clk(clk), .din(write_data),
    .dout(ram_13_dout), .be3(multiplexer_3_out[0]), .be2(multiplexer_3_out[1]), .be1(multiplexer_3_out[2]),
    .be0(multiplexer_3_out[3]));
  not not_13 (not_13_out, demultiplexer_1_out12);
  RAM #(.addrWidth(24), .dataWidth(32), .databus("bibus"), .byteenables("byteEnables")) ram_14 (
    .addr(mem_sel[25:2]), .we(demultiplexer_1_out13), .oe(not_14_out), .clk(clk), .din(write_data),
    .dout(ram_14_dout), .be3(multiplexer_3_out[0]), .be2(multiplexer_3_out[1]), .be1(multiplexer_3_out[2]),
    .be0(multiplexer_3_out[3]));
  not not_14 (not_14_out, demultiplexer_1_out13);
  RAM #(.addrWidth(24), .dataWidth(32), .databus("bibus"), .byteenables("byteEnables")) ram_15 (
    .addr(mem_sel[25:2]), .we(demultiplexer_1_out14), .oe(not_15_out), .clk(clk), .din(write_data),
    .dout(ram_15_dout), .be3(multiplexer_3_out[0]), .be2(multiplexer_3_out[1]), .be1(multiplexer_3_out[2]),
    .be0(multiplexer_3_out[3]));
  not not_15 (not_15_out, demultiplexer_1_out14);
  RAM #(.addrWidth(24), .dataWidth(32), .databus("bibus"), .byteenables("byteEnables")) ram_16 (
    .addr(mem_sel[25:2]), .we(demultiplexer_1_out15), .oe(not_16_out), .clk(clk), .din(write_data),
    .dout(ram_16_dout), .be3(multiplexer_3_out[0]), .be2(multiplexer_3_out[1]), .be1(multiplexer_3_out[2]),
    .be0(multiplexer_3_out[3]));
  not not_16 (not_16_out, demultiplexer_1_out15);
  Multiplexer #(.select(4), .width(32), .enable("false")) multiplexer_4 (
    .in0(ram_1_dout), .in1(ram_2_dout), .in2(ram_3_dout), .in3(ram_4_dout), .in4(ram_5_dout),
    .in5(ram_6_dout), .in6(ram_7_dout), .in7(ram_8_dout), .in8(ram_9_dout), .in9(ram_10_dout),
    .in10(ram_11_dout), .in11(ram_12_dout), .in12(ram_13_dout), .in13(ram_14_dout), .in14(ram_15_dout),
    .in15(ram_16_dout), .out(read_data), .sel(sel));

  // Other names for the same wires on the sheet: mem_sel_t[23:0] = mem_sel[25:2]
endmodule

module Logic (
  input  [31:0] a,
  input  [31:0] b,
  input  [1:0] sel,
  output [31:0] d_out
);

  wire [31:0] and_1_out, nor_1_out, or_1_out, xor_1_out;

  assign and_1_out = a & b;  // AND_Gate and_1, 32 bits wide
  assign or_1_out = a | b;  // OR_Gate or_1, 32 bits wide
  assign nor_1_out = ~(a | b);  // NOR_Gate nor_1, 32 bits wide
  assign xor_1_out = a ^ b;  // XOR_Gate xor_1, 32 bits wide
  Multiplexer #(.select(2), .width(32), .enable("false")) multiplexer_1 (
    .in0(and_1_out), .in1(or_1_out), .in2(nor_1_out), .in3(xor_1_out), .out(d_out), .sel(sel));
endmodule

module ShifterUnit (
  input  [31:0] a,
  input  [1:0] op,
  input  [31:0] amt,
  output [31:0] d_out
);

  wire [31:0] shifter_1_out, shifter_2_out, shifter_3_out;

  Shifter #(.width(32)) shifter_1 (.in(a), .\dist (amt[4:0]), .out(shifter_1_out));
  Shifter #(.width(32), .shift("lr")) shifter_2 (.in(a), .\dist (amt[4:0]), .out(shifter_2_out));
  Shifter #(.width(32), .shift("ar")) shifter_3 (.in(a), .\dist (amt[4:0]), .out(shifter_3_out));
  Multiplexer #(.select(2), .width(32), .enable("false")) multiplexer_1 (
    .in0(shifter_1_out), .in1(shifter_2_out), .in2(shifter_3_out), .out(d_out), .sel(op));  // open: in3
endmodule

module z32B_AdderOverflow (
  input  [31:0] a,
  input  c_in,
  input  [31:0] b,
  output overflow,
  output [31:0] sum,
  output c_out
);

  wire z1b_adder_1_c_out, z1b_adder_2_c_out, z1b_adder_3_c_out, z1b_adder_4_c_out, z1b_adder_5_c_out,
       z1b_adder_6_c_out, z1b_adder_7_c_out, z1b_adder_8_c_out, z1b_adder_9_c_out, z1b_adder_10_c_out,
       z1b_adder_11_c_out, z1b_adder_12_c_out, z1b_adder_13_c_out, z1b_adder_14_c_out, z1b_adder_15_c_out,
       z1b_adder_16_c_out, z1b_adder_17_c_out, z1b_adder_18_c_out, z1b_adder_19_c_out, z1b_adder_20_c_out,
       z1b_adder_21_c_out, z1b_adder_22_c_out, z1b_adder_23_c_out, z1b_adder_24_c_out, z1b_adder_25_c_out,
       z1b_adder_26_c_out, z1b_adder_27_c_out, z1b_adder_28_c_out, z1b_adder_29_c_out, z1b_adder_30_c_out,
       z1b_adder_31_c_out;

  z1B_Adder z1b_adder_1 (.a(a[0]), .b(c_in), .c_in(b[0]), .sum(sum[0]), .c_out(z1b_adder_1_c_out));
  z1B_Adder z1b_adder_2 (.a(a[1]), .b(b[1]), .c_in(z1b_adder_1_c_out), .sum(sum[1]), .c_out(z1b_adder_2_c_out));
  z1B_Adder z1b_adder_3 (.a(a[2]), .b(b[2]), .c_in(z1b_adder_2_c_out), .sum(sum[2]), .c_out(z1b_adder_3_c_out));
  z1B_Adder z1b_adder_4 (.a(a[3]), .b(b[3]), .c_in(z1b_adder_3_c_out), .sum(sum[3]), .c_out(z1b_adder_4_c_out));
  z1B_Adder z1b_adder_5 (.a(a[4]), .b(b[4]), .c_in(z1b_adder_4_c_out), .sum(sum[4]), .c_out(z1b_adder_5_c_out));
  z1B_Adder z1b_adder_6 (.a(a[5]), .b(b[5]), .c_in(z1b_adder_5_c_out), .sum(sum[5]), .c_out(z1b_adder_6_c_out));
  z1B_Adder z1b_adder_7 (.a(a[6]), .b(b[6]), .c_in(z1b_adder_6_c_out), .sum(sum[6]), .c_out(z1b_adder_7_c_out));
  z1B_Adder z1b_adder_8 (.a(a[7]), .b(b[7]), .c_in(z1b_adder_7_c_out), .sum(sum[7]), .c_out(z1b_adder_8_c_out));
  z1B_Adder z1b_adder_9 (.a(a[8]), .b(b[8]), .c_in(z1b_adder_8_c_out), .sum(sum[8]), .c_out(z1b_adder_9_c_out));
  z1B_Adder z1b_adder_10 (.a(a[9]), .b(b[9]), .c_in(z1b_adder_9_c_out), .sum(sum[9]), .c_out(z1b_adder_10_c_out));
  z1B_Adder z1b_adder_11 (.a(a[10]), .b(b[10]), .c_in(z1b_adder_10_c_out), .sum(sum[10]), .c_out(z1b_adder_11_c_out));
  z1B_Adder z1b_adder_12 (.a(a[11]), .b(b[11]), .c_in(z1b_adder_11_c_out), .sum(sum[11]), .c_out(z1b_adder_12_c_out));
  z1B_Adder z1b_adder_13 (.a(a[12]), .b(b[12]), .c_in(z1b_adder_12_c_out), .sum(sum[12]), .c_out(z1b_adder_13_c_out));
  z1B_Adder z1b_adder_14 (.a(a[13]), .b(b[13]), .c_in(z1b_adder_13_c_out), .sum(sum[13]), .c_out(z1b_adder_14_c_out));
  z1B_Adder z1b_adder_15 (.a(a[14]), .b(b[14]), .c_in(z1b_adder_14_c_out), .sum(sum[14]), .c_out(z1b_adder_15_c_out));
  z1B_Adder z1b_adder_16 (.a(a[15]), .b(b[15]), .c_in(z1b_adder_15_c_out), .sum(sum[15]), .c_out(z1b_adder_16_c_out));
  z1B_Adder z1b_adder_17 (.a(a[16]), .b(b[16]), .c_in(z1b_adder_16_c_out), .sum(sum[16]), .c_out(z1b_adder_17_c_out));
  z1B_Adder z1b_adder_18 (.a(a[17]), .b(b[17]), .c_in(z1b_adder_17_c_out), .sum(sum[17]), .c_out(z1b_adder_18_c_out));
  z1B_Adder z1b_adder_19 (.a(a[18]), .b(b[18]), .c_in(z1b_adder_18_c_out), .sum(sum[18]), .c_out(z1b_adder_19_c_out));
  z1B_Adder z1b_adder_20 (.a(a[19]), .b(b[19]), .c_in(z1b_adder_19_c_out), .sum(sum[19]), .c_out(z1b_adder_20_c_out));
  z1B_Adder z1b_adder_21 (.a(a[20]), .b(b[20]), .c_in(z1b_adder_20_c_out), .sum(sum[20]), .c_out(z1b_adder_21_c_out));
  z1B_Adder z1b_adder_22 (.a(a[21]), .b(b[21]), .c_in(z1b_adder_21_c_out), .sum(sum[21]), .c_out(z1b_adder_22_c_out));
  z1B_Adder z1b_adder_23 (.a(a[22]), .b(b[22]), .c_in(z1b_adder_22_c_out), .sum(sum[22]), .c_out(z1b_adder_23_c_out));
  z1B_Adder z1b_adder_24 (.a(a[23]), .b(b[23]), .c_in(z1b_adder_23_c_out), .sum(sum[23]), .c_out(z1b_adder_24_c_out));
  z1B_Adder z1b_adder_25 (.a(a[24]), .b(b[24]), .c_in(z1b_adder_24_c_out), .sum(sum[24]), .c_out(z1b_adder_25_c_out));
  z1B_Adder z1b_adder_26 (.a(a[25]), .b(b[25]), .c_in(z1b_adder_25_c_out), .sum(sum[25]), .c_out(z1b_adder_26_c_out));
  z1B_Adder z1b_adder_27 (.a(a[26]), .b(b[26]), .c_in(z1b_adder_26_c_out), .sum(sum[26]), .c_out(z1b_adder_27_c_out));
  z1B_Adder z1b_adder_28 (.a(a[27]), .b(b[27]), .c_in(z1b_adder_27_c_out), .sum(sum[27]), .c_out(z1b_adder_28_c_out));
  z1B_Adder z1b_adder_29 (.a(a[28]), .b(b[28]), .c_in(z1b_adder_28_c_out), .sum(sum[28]), .c_out(z1b_adder_29_c_out));
  z1B_Adder z1b_adder_30 (.a(a[29]), .b(b[29]), .c_in(z1b_adder_29_c_out), .sum(sum[29]), .c_out(z1b_adder_30_c_out));
  z1B_Adder z1b_adder_31 (.a(a[30]), .b(b[30]), .c_in(z1b_adder_30_c_out), .sum(sum[30]), .c_out(z1b_adder_31_c_out));
  z1B_Adder z1b_adder_32 (.a(a[31]), .b(b[31]), .c_in(z1b_adder_31_c_out), .sum(sum[31]), .c_out(c_out));
  xor xor_1 (overflow, c_out, z1b_adder_31_c_out);
endmodule

module ComparatorUnit (
  input  [31:0] a,
  input  [31:0] b,
  input  sub_control,
  output [31:0] sum,
  output overflow,
  output comp
);

  wire z32b_adderoverflow_2_c_out, z32b_adderoverflow_2_overflow;

  z32B_AdderOverflow z32b_adderoverflow_1 (
    .sum(sum), .overflow(overflow), .b(b), .c_in(sub_control), .a(a));  // open: c_out
  z32B_AdderOverflow z32b_adderoverflow_2 (
    .overflow(z32b_adderoverflow_2_overflow), .b(b), .c_in(1'b1), .a(a), .c_out(z32b_adderoverflow_2_c_out));  // open: sum
  xor xor_1 (comp, z32b_adderoverflow_2_c_out, z32b_adderoverflow_2_overflow);
endmodule

module z28x4Mem (
  input  [31:0] addr,
  input  write_enable,
  input  [31:0] write_data,
  input  [1:0] access_size,
  input  clk,
  output [31:0] read_data
);

  wire demultiplexer_1_out0, demultiplexer_1_out1, demultiplexer_1_out2, demultiplexer_1_out3, not_1_out;
  wire [31:0] z24x16mem_1_read_data, z24x16mem_2_read_data, z24x16mem_3_read_data, z24x16mem_4_read_data;

  Demultiplexer #(.select(2), .enable("false")) demultiplexer_1 (
    .out0(demultiplexer_1_out0), .out1(demultiplexer_1_out1), .out2(demultiplexer_1_out2),
    .out3(demultiplexer_1_out3), .in(not_1_out), .sel(addr[31:30]));
  not not_1 (not_1_out, write_enable);
  z24x16Mem z24x16mem_1 (
    .wr_enable(demultiplexer_1_out0), .mem_sel(addr[25:0]), .sel(addr[29:26]), .write_data(write_data),
    .clk(clk), .access_size(access_size), .read_data(z24x16mem_1_read_data));
  z24x16Mem z24x16mem_2 (
    .wr_enable(demultiplexer_1_out1), .mem_sel(addr[25:0]), .sel(addr[29:26]), .write_data(write_data),
    .clk(clk), .access_size(access_size), .read_data(z24x16mem_2_read_data));
  z24x16Mem z24x16mem_3 (
    .wr_enable(demultiplexer_1_out2), .mem_sel(addr[25:0]), .sel(addr[29:26]), .write_data(write_data),
    .clk(clk), .access_size(access_size), .read_data(z24x16mem_3_read_data));
  z24x16Mem z24x16mem_4 (
    .wr_enable(demultiplexer_1_out3), .mem_sel(addr[25:0]), .sel(addr[29:26]), .write_data(write_data),
    .clk(clk), .access_size(access_size), .read_data(z24x16mem_4_read_data));
  Multiplexer #(.select(2), .width(32), .enable("false")) multiplexer_1 (
    .in0(z24x16mem_1_read_data), .in1(z24x16mem_2_read_data), .in2(z24x16mem_3_read_data),
    .in3(z24x16mem_4_read_data), .out(read_data), .sel(addr[31:30]));
endmodule
